// Digital circuit arquivoPrincipalROM.dig as structural Verilog
module arquivoPrincipalROM (
  output O0,
  output O1,
  output O2,
  output O3
);

  blocoROM blocorom_1 (
    .B00(1'b1), .B01(1'b0), .B02(1'b0), .B03(1'b0), .B10(1'b1), .B11(1'b0), .B12(1'b1), .B13(1'b0),
    .B20(1'b1), .B21(1'b0), .B22(1'b0), .B23(1'b1), .B30(1'b0), .B31(1'b0), .B32(1'b0), .B33(1'b0), .O0(O0),
    .O1(O1), .O2(O2), .O3(O3));  // open: L0, L1, L2, L3
  blocoROM blocorom_2 (
    .B00(1'b0), .B01(1'b0), .B02(1'b0), .B03(1'b1), .B10(1'b0), .B11(1'b1), .B12(1'b0), .B13(1'b1),
    .B20(1'b1), .B21(1'b0), .B22(1'b1), .B23(1'b1), .B30(1'b0), .B31(1'b0), .B32(1'b0), .B33(1'b1), .O0(O0),
    .O1(O1), .O2(O2), .O3(O3));  // open: L0, L1, L2, L3
  blocoROM blocorom_3 (
    .B00(1'b1), .B01(1'b0), .B02(1'b0), .B03(1'b1), .B10(1'b0), .B11(1'b1), .B12(1'b0), .B13(1'b1),
    .B20(1'b1), .B21(1'b0), .B22(1'b0), .B23(1'b1), .B30(1'b0), .B31(1'b0), .B32(1'b0), .B33(1'b0), .O0(O0),
    .O1(O1), .O2(O2), .O3(O3));  // open: L0, L1, L2, L3
  blocoROM blocorom_4 (
    .B00(1'b0), .B01(1'b0), .B02(1'b0), .B03(1'b1), .B10(1'b0), .B11(1'b1), .B12(1'b0), .B13(1'b1),
    .B20(1'b1), .B21(1'b0), .B22(1'b0), .B23(1'b1), .B30(1'b0), .B31(1'b0), .B32(1'b0), .B33(1'b0), .O0(O0),
    .O1(O1), .O2(O2), .O3(O3));  // open: L0, L1, L2, L3
endmodule
