// Digital circuit bloco4bits.dig as structural Verilog
module bloco4bits (
  input  In0,
  input  In1,
  input  In2,
  input  In3,
  input  L,
  output Out0,
  output Out1,
  output Out2,
  output Out3
);

  assign Out0 = L ? In0 : 1'bz;  // Driver driver_1
  assign Out1 = L ? In1 : 1'bz;  // Driver driver_2
  assign Out2 = L ? In2 : 1'bz;  // Driver driver_3
  assign Out3 = L ? In3 : 1'bz;  // Driver driver_4
endmodule
