// Digital circuit 4BitAdder.dig as structural Verilog
module _4BitAdder (
  input  Ci,
  input  X3,
  input  X2,
  input  X1,
  input  X0,
  input  Y3,
  input  Y2,
  input  Y1,
  input  Y0,
  output O3,
  output O2,
  output O1,
  output O0,
  output Co,
  output OF,
  output Zr
);

  wire adder_1_ti_plus_1, adder_2_ti_plus_1, adder_3_ti_plus_1;

  Adder adder_1 (.Ai(X3), .Bi(Y3), .Ti(Ci), .Oi(O3), .Ti_plus_1(adder_1_ti_plus_1));
  Adder adder_2 (.Ai(X2), .Bi(Y2), .Ti(adder_1_ti_plus_1), .Oi(O2), .Ti_plus_1(adder_2_ti_plus_1));
  Adder adder_3 (.Ai(X1), .Bi(Y1), .Ti(adder_2_ti_plus_1), .Oi(O1), .Ti_plus_1(adder_3_ti_plus_1));
  Adder adder_4 (.Ai(X0), .Bi(Y0), .Ti(adder_3_ti_plus_1), .Oi(O0), .Ti_plus_1(Co));
  xor xor_1 (OF, O1, O0);
  nor nor_1 (Zr, O3, O2, O1, O0);
endmodule
