// Digital circuit BlocoComplemento.dig as structural Verilog
module BlocoComplemento (
  input  I0,
  input  I1,
  input  I2,
  input  I3,
  input  E,
  output O0,
  output O1,
  output O2,
  output O3
);

  wire not_1_out, not_2_out, not_3_out, not_4_out, not_5_out;

  not not_1 (not_1_out, E);
  not not_2 (not_2_out, I0);
  not not_3 (not_3_out, I1);
  not not_4 (not_4_out, I2);
  not not_5 (not_5_out, I3);
  assign O0 = E ? not_2_out : 1'bz;  // Driver driver_1
  assign O0 = not_1_out ? I0 : 1'bz;  // Driver driver_2
  assign O1 = E ? not_3_out : 1'bz;  // Driver driver_3
  assign O1 = not_1_out ? I1 : 1'bz;  // Driver driver_4
  assign O2 = E ? not_4_out : 1'bz;  // Driver driver_5
  assign O2 = not_1_out ? I2 : 1'bz;  // Driver driver_6
  assign O3 = E ? not_5_out : 1'bz;  // Driver driver_7
  assign O3 = not_1_out ? I3 : 1'bz;  // Driver driver_8
endmodule
